# Fritzing sketch SusenjeCevki - Breadboard (saved by Fritzing 0.9.3b)
breadboards: 1

parts:
  Part1 = Arduino Uno (Rev3)
  R1 = Resistor [tolerance=±5% resistance=1k package="2512 [SMD]"]
  Ventilator = DC Motor
  Q1 = NPN-Transistor [package="SOT-23 [SMD]"]

nets:
  N1: Part1.D8, R1.Pin_1
  N2: Part1.GND, Q1.1
  N3: Part1.VIN, Ventilator.pin_1
  N4: R1.Pin_0, Q1.0
  N5: Ventilator.pin_2, Q1.2
