# Fritzing sketch SusenjeCevki - PCB (saved by Fritzing 0.9.3b)

parts:
  Ventilator = DC Motor
  J2 = female pin header, 3 pins [form="♀ (female)"]
  Part1 = Arduino Uno (Rev3)
  Q1 = NPN-Transistor [package="SOT-23 [SMD]"]
  J1 = male pin header, 2 pins [form="♂ (male)"]
  R1 = Resistor [tolerance=±5% resistance=1k package="2512 [SMD]"]

nets:
  N1: Ventilator.pin_1, Q1.1, J1.pin1
  N2: Ventilator.pin_2, J2.pin3, Part1.VIN, J1.pin2
  N3: J2.pin1, Part1.GND, Q1.2
  N4: J2.pin2, Part1.D8, R1.Pin_1
  N5: Q1.0, R1.Pin_0
